# Fritzing sketch SmartBikeLight (saved by Fritzing 0.9.10b)

parts:
  BAT1 = Battery Holders [package=battery-aaa]
  Adafruit_MAX1 = Adafruit MAX17048 LiPoly / LiIon Fuel Gauge and Battery Monitor [part_number=#5580]
  Part1 = Adafruit ADXL345 [part_number="Adafruit #1231"]
  GY-NEO6MV3 = SUP500F [package=sup500f]
  TP1 = TP4056 [chip_label=TP4056 package="DIP (Dual Inline) [THT]"]  # not connected
  S1 = SWITCH-MOMENTARY-2 [package=tactile-pth]  # not connected
  S2 = Toggle Switch [package=THT]
  IC1 = Voltage Regulator [package=to-220-alt]
  Part2 = Matrix LED de 8x8 basada en MAX7219
  R3 = Resistor [tolerance=±5% power=0.25 resistance=220 package=THT]  # not connected
  U3 = LoRaWAN RN2483/RN2903 Breakout board
  ANT1 = Antenna
  J$1 = SMA Antenna Connector [package=sma-edge]
  R12 = Resistor [tolerance=±5% resistance=220 package="2010 [SMD]"]
  R14 = Photocell (LDR) [package=THT]
  U4 = LuaNode32 / ESP32 [part_number=ESP32S-PIN30]
  a1 = LED - 5mm [color="Red (633nm)" current=0.030 package="5 mm [THT]"]  # not connected
  R13 = Resistor [tolerance=±5% power=0.25 resistance=220 package=THT]

nets:
  N1: BAT1.-, Adafruit_MAX1.GND, S2.COM, IC1.IN
  N2: BAT1.+, Adafruit_MAX1.VCC, Adafruit_MAX1.VBAT, S2.L2, IC1.OUT
  N3: Adafruit_MAX1.SCL, Part1.SCL, U4.D22
  N4: Adafruit_MAX1.SDA, Part1.SDA/SDIO
  N5: Part1.VIN, R14.pin_1
  N6: Part1.GND, R13.Pin_0
  N7: GY-NEO6MV3.RX-I, U4.TX2
  N8: GY-NEO6MV3.TX-O, U4.RX2
  N9: Part2.CS, U4.D12
  N10: Part2.CLK, U4.D13
  N11: Part2.DIN, U4.D14
  N12: U3.RST, U4.D4
  N13: U3.RX, U4.D18
  N14: U3.TX, U4.D19
  N15: ANT1.antenna_lead, J$1.GND
  N16: R12.Pin_0, U4.GND
  N17: R12.Pin_1, U4.D2
  N18: R14.pin_0, U4.D34, R13.Pin_1

notes:
  Smart Bike Light

custom parts:
  Adafruit MAX17048 LiPoly / LiIon Fuel Gauge and Battery Monitor: Low cost Lithium Polymer batteries have revolutionized electronics - they're thin, they're light, they can be regulated down to 3.3V and they're easy to charge. On your phone, there's a little image of a battery cell that tells you the percentage of charge - so you know when you absolutely need to plug it in and when you can stay untethered. The Adafruit MAX17048 LiPoly / LiIon Fuel Gauge and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
  Adafruit ADXL345: Filling out our accelerometer offerings, we now have the really lovely digital ADXL345 from Analog Devices, a triple-axis accelerometer with digital I2C and SPI interface breakout. We added an on-board 3.3V regulator and logic-level shifting circuitry, making it a perfect choice for interfacing with any 3V or 5V microcontroller such as the Arduino. The sensor has three axes of measurements, X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
  TP4056: A DIP stand-in part for whatever IC you want. With 6 pins on a 300mil dual inline package (DIP) footprint.
  LoRaWAN RN2483/RN2903 Breakout board: This breakout board offers an affordable solution for makers working with the popular RN2483A and RN2903A LoRa transceivers from Microchip, widely used for LoRaWAN (Commonly called just RN2483 and RN2903, or collectively, RN2xx3). The layout of this breakout board is based on the the datasheet reference designs. This board breaks out all 14 GPIO pins to a row of 0.1" pin header, and the power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
  LuaNode32 / ESP32: New Image for LuaNode32 DOIT ESP32 DEVKIT V1. Base parts from LuaNode32 / ESP32 ESP32 based LuaNode32 by G.Noorlander DOIT Esp32 DevKit v1 (30 pins long, 11 pins width) by Werner Rothschopf (modified by vanepp Dec 2018)
